// Logisim project DathaPath.circ as structural Verilog: 2 circuits, main circuit DathaPath
module DathaPath (
  input  [31:0] in_1,
  input  [31:0] in_2,
  input  [31:0] in_3,
  input  [31:0] in_4,
  input  PCWrite,
  input  IorD,
  input  IRWrite,
  input  CLK,
  input  RST
);

  wire NF, undriven, ZF;
  wire [4:0] Dir_Rs, Dir_Rt;
  wire [15:0] offset;
  wire [25:0] Dir_Salto;
  wire [31:0] A, A_out, ALU_Out, B, B_out, Data_out, Instr_q, instruction_data_memory_1_out_5,
       multiplexer_1_out, offset_ext, PC, PC_prime, ZF_result_low;

  Multiplexer #(.width(32), .enable("false")) multiplexer_1 (
    .in0(PC), .in1(ALU_Out), .out(multiplexer_1_out), .sel(IorD));
  Instruction_Data_Memory instruction_data_memory_1 (
    .in_3(multiplexer_1_out), .out_5(instruction_data_memory_1_out_5), .in_1(CLK), .in_2(undriven));  // open: in_4
  Register #(.width(32)) u_PC (.D(PC_prime), .en(PCWrite), .Q(PC), .clk(CLK), .clr(RST));
  Register #(.width(32)) Instr (
    .D(instruction_data_memory_1_out_5), .en(IRWrite), .Q(Instr_q), .clk(CLK));  // open: clr
  Register #(.width(32)) Data (.D(instruction_data_memory_1_out_5), .Q(Data_out), .clk(CLK));  // open: en, clr
  Branch_Control branch_control_1 (
    .N(NF), .Z(ZF), .PC(PC), .PC_prime(PC_prime), .Constant_extended(offset_ext), .Destiny(Dir_Salto),
    .Register(A));  // open: j, Branch_Code
  Instruction_Decoder instruction_decoder_1 (
    .Instruction(Instr_q), .out_2(Dir_Salto), .out_4(Dir_Rt), .out_3(Dir_Rs), .out_6(offset));  // open: out_5, out_7, out_8
  assign offset_ext = {{16{1'b0}}, offset};  // Bit_Extender bit_extender_1
  Register_File_CPU_main main_1 (
    .\Dirección_de_destino (Dir_Rt), .Datos_de_entrada(Data_out), .Selector_Salida_A(Dir_Rs), .Clock(CLK),
    .Salida_A(A_out), .Salida_B(B_out));  // open: R_W, Selector_Salida_B, Reset, HI_in, LO_in, R_W_HI_LO, out_13, out_14
  Register #(.width(32)) u_A (.D(A_out), .Q(A), .clk(CLK));  // open: en, clr
  Register #(.width(32)) u_B (.D(B_out), .Q(B), .clk(CLK));  // open: en, clr
  ALU u_ZF (.Input_0(A), .Input_1(offset_ext), .Result_Low(ZF_result_low), .ZF(ZF), .NF(NF));  // open: OpCode, High
  Register #(.width(32)) u_ALU_Out (.D(ZF_result_low), .Q(ALU_Out), .clk(CLK));  // open: en, clr

  // Other names for the same wires on the sheet: I0[31:0] = in_1; I1[31:0] = in_3; I2[31:0] = in_2; I3[31:0] = in_4
endmodule

module Instruction_Data_Memory (
  input  in_1,
  input  in_2,
  input  [31:0] in_3,
  input  [31:0] in_4,
  output [31:0] out_5
);


  // Other names for the same wires on the sheet: Address[31:0] = in_3; CLK = in_1; RD[31:0] = out_5; WD[31:0] = in_4;
  //   WE = in_2
endmodule
